# Fritzing sketch neuralearn (saved by Fritzing 1.0.6)
breadboards: 1

parts:
  A1 = ESP32-S3 Wroom board Freenove
  LCD1 = 2.8" SPI TFT Module [part_number=ILI9341]
  Part1 = INMP441
  Part2 = Adafruit MAX98357A I2S 3W Class D Amplifier [part_number=MAX98357A]
  SPKR1 = Loudspeaker
  U1 = LIPO-1000mAh [package=lipo-1000]
  U3 = POT [knob_status=50% power=0.5W package=pot_mammoth]
  S1 = Pushbutton [package="[SMD]"]
  TP1 = TP4056 [chip_label=TP4056 package="DIP (Dual Inline) [THT]"]
  R1 = Resistor [tolerance=±5% power=0.25W resistance=100k package=THT]
  R2 = Resistor [tolerance=±5% power=0.25W resistance=100k package=THT]
  R3 = Resistor [tolerance=±5% power=0.25W resistance=10k package=THT]

nets (from the schematic view):
  N1: A1.Pin_1, LCD1.pin1, LCD1.pin8, Part1.VDD, U3.S, R3.Pin_0
  N2: A1.Pin_13, LCD1.pin4
  N3: A1.Pin_19, LCD1.pin3
  N4: A1.Pin_20, Part2.VIN
  GND: A1.Pin_21, LCD1.pin2, Part1.L/R, Part1.GND, Part2.GND, U3.E, S1.Pin_1, S1.Pin_2
  N5: A1.Pin_24, LCD1.pin5
  N6: A1.Pin_25, Part1.SD
  N7: A1.Pin_26, LCD1.pin6
  N8: A1.Pin_27, LCD1.pin7
  N9: A1.Pin_28, S1.Pin_3, S1.Pin_4
  N10: A1.Pin_32, Part1.WS
  N11: A1.Pin_33, Part1.SCK
  N12: A1.Pin_34, Part2.DIN
  N13: A1.Pin_35, Part2.BCLK
  N14: A1.Pin_36, Part2.LRCLK
  N15: A1.Pin_37, U3.A
  N16: A1.Pin_38, R1.Pin_1, R2.Pin_0
  N17: Part2.SD_MODE, R3.Pin_1
  N18: Part2.VO-, SPKR1.pin2
  N19: Part2.VO+, SPKR1.pin1
  N20: U1.+, TP1.pin4
  N21: U1.-, TP1.pin5
  N22: TP1.pin3, R1.Pin_0
  N23: TP1.pin6, R2.Pin_1

custom parts:
  ESP32-S3 Wroom board Freenove: ESP32-S3-WROOM is a powerful and small controller with onboard wireless and camera.
  2.8" SPI TFT Module: A generic 2.8 inch LCD TFT 320x240 display with touchscreen and SD card slot. Uses the ILI9341 controller, like the Adafruit displays of this size uses.
  INMP441: This is a simple breakout board for the INMP441 I2S MEMS microphone.
  Adafruit MAX98357A I2S 3W Class D Amplifier: Listen to this good news - we now have an all in one digital audio amp breakout board that works incredibly well with the Raspberry Pi! If you're looking for an easy and low cost way to get you digital sound files bumpin' then the MAX08357 I2S Amp Breakout is for you. It takes standard I2S digital audio input and, not only decodes it into analog, but also amplifies it directly into a speaker.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
  TP4056: A DIP stand-in part for whatever IC you want. With 6 pins on a 300mil dual inline package (DIP) footprint.
